# Fritzing sketch FixtureInspector (saved by Fritzing 0.9.3b)

parts:
  Raspberry_Pi_1 = Raspberry Pi 3 [part_number=RPI-3-V1.2]
  M1 = Stepper Motor - Bipolar
  부품1 = 12 NeoPixel Ring [part_number=1643]  # not connected
  MD1 = Maker Drive
  Power_plug1 = Power plug

nets:
  N1: Raspberry_Pi_1.GPIO22, MD1.M2B_IO
  N2: Raspberry_Pi_1.GPIO25, MD1.M1A_IO
  N3: Raspberry_Pi_1.GPIO24, MD1.M1B_IO
  N4: Raspberry_Pi_1.GPIO23, MD1.M2A_IO
  GND: Raspberry_Pi_1.GND, Power_plug1.GND
  5V: Raspberry_Pi_1.5V, Power_plug1.VCC
  N5: M1.A, MD1.M2B
  N6: M1.C, MD1.M2A
  N7: M1.B, MD1.M1B
  N8: M1.D, MD1.M1A

custom parts:
  12 NeoPixel Ring: 12 ultra bright smart LED NeoPixels are arranged in a circle with 1.5" (37mm) outer diameter. The rings are 'chainable' - connect the output pin of one to the input pin of another. Use only one microcontroller pin to control as many as you can chain together! Each LED is addressable as the driver chip is inside the LED. Each one has ~18mA constant current drive so the color will be very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
  Maker Drive: Simplifying H-Bridge Motor Driver for Beginner.
